// Logisim project drisc.circ as structural Verilog: 16 circuits, main circuit main
module main (
);

  wire address_selector_1_read_out, address_selector_2_read_out, address_selector_2_write_out,
       address_selector_3_write_out, ALU_Use_PC, button_1_out, button_2_out, button_3_out, button_4_out,
       button_5_out, button_6_out, button_7_out, button_8_out, Cl0ck, Forward_Address, IO_Load, IO_Read_IO,
       IO_Write_IO, keyboard_1_avail, Load_Upper_Immediate, OperationController_pad_read,
       OperationController_pad_write, PAD_Write_Address, PC_Jump, PC_Read_Next, PC_Relative, PC_Use_Offset,
       Phase1, Phase3, Register_File_Write, Reset, shift_register_1_q1, undriven_3, Use_Immediate;
  wire [1:0] Data_Offset, OperationController_pad_data_size;
  wire [2:0] Funct3;
  wire [3:0] ALUComponent_cnzv, undriven, undriven_2;
  wire [4:0] OP_Function;
  wire [6:0] keyboard_1_data, OperationController_opcode;
  wire [7:0] controlled_buffer_1_out, controlled_buffer_1_out_2, controlled_buffer_1_out_3,
       controlled_buffer_1_out_4, s_r_ff_8_q;
  wire [7:7] not_1_out;
  wire [14:0] Register_Addresses;
  wire [15:0] random_1_out;
  wire [31:0] address_selector_2_address_out, address_selector_3_address_out, ALUComponent_result,
       ALUComponent_source1, ALUComponent_source2, DataIO_cpu_out, DataIO_io_out, Immediate,
       Memory_Address_q, multiplexer_1_out, multiplexer_2_out, multiplexer_3_out,
       ProgramCounter_address_bus_out, ProgramCounter_current_out, ProgramCounter_next_out,
       RegisterFile_a_bus_out, RegisterFile_b_bus_out;

  // Probe on Register_Addresses[4:0]
  // Probe on Register_Addresses[9:5]
  // Probe on Register_Addresses[14:10]
  Register_File RegisterFile (
    .C_Bus_In(multiplexer_1_out), .Addresses_In(Register_Addresses), .Write(Register_File_Write),
    .Clock(Cl0ck), .Reset(Reset), .A_Bus_Out(RegisterFile_a_bus_out), .B_Bus_Out(RegisterFile_b_bus_out));
  // Probe on RegisterFile_a_bus_out
  // Probe on RegisterFile_b_bus_out
  // Probe on multiplexer_1_out
  assign {controlled_buffer_1_out_4, controlled_buffer_1_out_3, controlled_buffer_1_out_2, controlled_buffer_1_out} = IO_Read_IO ? DataIO_io_out : 32'bz;  // Controlled_Buffer controlled_buffer_1
  Multiplexer #(.width(32)) multiplexer_1 (
    .in0(multiplexer_2_out), .in1(DataIO_cpu_out), .out(multiplexer_1_out), .sel(IO_Load));
  Data_Input_Output DataIO (
    .Store(Phase1),
    .IO_In({controlled_buffer_1_out_4, controlled_buffer_1_out_3, controlled_buffer_1_out_2, controlled_buffer_1_out}),
    .Load(IO_Write_IO), .Clock(Cl0ck), .Data_Offset(Data_Offset), .Data_Type(Funct3),
    .CPU_In(RegisterFile_b_bus_out), .CPU_Out(DataIO_cpu_out), .IO_Out(DataIO_io_out));
  Multiplexer #(.width(32)) multiplexer_2 (
    .in0(multiplexer_3_out), .in1(Immediate), .out(multiplexer_2_out), .sel(Load_Upper_Immediate));
  // Probe on ALUComponent_source1
  // Probe on ALUComponent_source2
  ALU ALUComponent (
    .Operation(OP_Function), .Use_PC(ALU_Use_PC), .Use_Immediate(Use_Immediate), .a(RegisterFile_a_bus_out),
    .Program_Counter_In(ProgramCounter_current_out), .b(RegisterFile_b_bus_out), .Immediate(Immediate),
    .Result(ALUComponent_result), .CNZV(ALUComponent_cnzv), .Source1(ALUComponent_source1),
    .Source2(ALUComponent_source2));
  Multiplexer #(.width(32)) multiplexer_3 (
    .in0(ALUComponent_result), .in1(ProgramCounter_next_out), .out(multiplexer_3_out), .sel(PC_Read_Next));
  Shift_Register #(.length(3)) shift_register_1 (
    .shift(1'b1), .in(Phase3), .clk(Cl0ck), .out(Phase3), .load(Reset), .d0(1'b0), .q0(Phase1), .d1(1'b1),
    .q1(shift_register_1_q1), .d2(1'b0));  // open: clr, q2
  Operation_Controller OperationController (
    .Phase1(Phase1), .Phase2(shift_register_1_q1), .Phase3(Phase3), .CNZV(ALUComponent_cnzv), .Clock(Cl0ck),
    .Reset(Reset),
    .Data_In({controlled_buffer_1_out_4, controlled_buffer_1_out_3, controlled_buffer_1_out_2, controlled_buffer_1_out}),
    .OPCode(OperationController_opcode), .Register_Adresses(Register_Addresses), .Funct3(Funct3),
    .Immediate(Immediate), .PC_Use_Offset(PC_Use_Offset), .PC_Forward_Address(Forward_Address),
    .Register_File_Write(Register_File_Write), .PC_Read_Next(PC_Read_Next), .PC_Relative(PC_Relative),
    .Load_Upper_Immediate(Load_Upper_Immediate), .PC_Jump(PC_Jump), .Use_Immediate(Use_Immediate),
    .ALU_Use_PC(ALU_Use_PC), .PAD_Write_Address(PAD_Write_Address), .Data_IO_Write_IO(IO_Write_IO),
    .OP_Function(OP_Function), .PAD_Read(OperationController_pad_read), .Data_IO_Read_IO(IO_Read_IO),
    .PAD_Data_Size(OperationController_pad_data_size), .PAD_Write(OperationController_pad_write),
    .IO_Load(IO_Load));
  // Probe on OperationController_opcode
  // Probe on Immediate
  // Probe on ProgramCounter_current_out
  Program_Counter ProgramCounter (
    .PC_Relative(PC_Relative), .Address_In(RegisterFile_a_bus_out), .Immediate(Immediate), .Jump(PC_Jump),
    .Reset(Reset), .Clock(Cl0ck), .Write(Phase3), .Use_Offset(PC_Use_Offset),
    .Forward_Address(Forward_Address), .Byte_Offset(Data_Offset),
    .Address_Bus_Out(ProgramCounter_address_bus_out), .Next_Out(ProgramCounter_next_out),
    .Current_Out(ProgramCounter_current_out));  // open: Last_Out
  // Probe on {controlled_buffer_1_out_4, controlled_buffer_1_out_3, controlled_buffer_1_out_2, controlled_buffer_1_out}
  // Probe on ProgramCounter_address_bus_out
  Clock MainClock (.out(Cl0ck));
  POR #(.PorHighDuration(1), .porsize(2)) por_1 (.out(Reset));
  Register #(.width(32)) Memory_Address (
    .D(ProgramCounter_address_bus_out), .en(PAD_Write_Address), .Q(Memory_Address_q), .clk(Cl0ck), .clr(Reset));
  Keyboard keyboard_1 (
    .clk(Cl0ck), .re(address_selector_1_read_out), .avail(keyboard_1_avail), .data(keyboard_1_data));  // open: clr
  Address_Selector address_selector_1 (
    .Read_In(OperationController_pad_read), .Write_In(OperationController_pad_write),
    .Address_In(Memory_Address_q), .Min_Address(32'hfffffc), .Max_Address(32'h1000000),
    .Read_Out(address_selector_1_read_out));  // open: Write_Out, Address_Out
  Address_Selector address_selector_2 (
    .Read_In(OperationController_pad_read), .Write_In(OperationController_pad_write),
    .Address_In(Memory_Address_q), .Min_Address({32{1'b0}}), .Max_Address(32'hfffffc),
    .Read_Out(address_selector_2_read_out), .Write_Out(address_selector_2_write_out),
    .Address_Out(address_selector_2_address_out));
  // RAM #(.addrWidth(24), .databus("bidir"), .enables("line"), .line("quad"), .misaligned("true"), .\type ("nonvolatile")) ram_1: pin names not known; wires that end beside it: address_selector_2_address_out[23:0], address_selector_2_write_out, address_selector_2_read_out, 1'b1, OperationController_pad_data_size[1], Cl0ck
  Address_Selector address_selector_3 (
    .Write_In(OperationController_pad_write), .Address_In(Memory_Address_q), .Min_Address(32'h1000000),
    .Max_Address(32'h1100000), .Write_Out(address_selector_3_write_out),
    .Address_Out(address_selector_3_address_out));  // open: Read_In, Read_Out
  not not_1 (not_1_out[7], keyboard_1_avail);
  Joystick joystick_1 ();  // open: x, y
  assign {controlled_buffer_1_out_4, controlled_buffer_1_out_3, controlled_buffer_1_out_2, controlled_buffer_1_out} = address_selector_1_read_out ? {not_1_out[7], keyboard_1_data, undriven_2, undriven, random_1_out} : 32'bz;  // Controlled_Buffer controlled_buffer_2
  Random random_1 (.next(address_selector_1_read_out), .clk(Cl0ck), .out(random_1_out[7:0]));  // open: clr
  // DipSwitch dipswitch_1: pin names not known
  // RGB_Video #(.cursor("No Cursor"), .height(64), .scale(6), .width(64)) rgb_video_1: pin names not known; wires that end beside it: Reset, Cl0ck, address_selector_3_write_out, address_selector_3_address_out[5:0], address_selector_3_address_out[11:6], {controlled_buffer_1_out_3, controlled_buffer_1_out_2, controlled_buffer_1_out}
  Button button_1 (.out(button_1_out));
  Button button_2 (.out(button_2_out));
  S_R_Flip_Flop #(.trigger("high")) s_r_ff_1 (
    .S(button_1_out), .clk(Cl0ck), .R(undriven_3), .Q(s_r_ff_8_q[7]), .reset(Reset));  // open: Qn, preset
  S_R_Flip_Flop #(.trigger("high")) s_r_ff_2 (
    .S(button_2_out), .clk(Cl0ck), .R(undriven_3), .Q(s_r_ff_8_q[6]), .reset(Reset));  // open: Qn, preset
  Button button_3 (.out(button_3_out));
  Button button_4 (.out(button_4_out));
  S_R_Flip_Flop #(.trigger("high")) s_r_ff_3 (
    .S(button_3_out), .clk(Cl0ck), .R(undriven_3), .Q(s_r_ff_8_q[5]), .reset(Reset));  // open: Qn, preset
  Button button_5 (.out(button_5_out));
  S_R_Flip_Flop #(.trigger("high")) s_r_ff_4 (
    .S(button_4_out), .clk(Cl0ck), .R(undriven_3), .Q(s_r_ff_8_q[4]), .reset(Reset));  // open: Qn, preset
  Button button_6 (.out(button_6_out));
  S_R_Flip_Flop #(.trigger("high")) s_r_ff_5 (
    .S(button_5_out), .clk(Cl0ck), .R(undriven_3), .Q(s_r_ff_8_q[3]), .reset(Reset));  // open: Qn, preset
  S_R_Flip_Flop #(.trigger("high")) s_r_ff_6 (
    .S(button_6_out), .clk(Cl0ck), .R(undriven_3), .Q(s_r_ff_8_q[2]), .reset(Reset));  // open: Qn, preset
  Button button_7 (.out(button_7_out));
  Button button_8 (.out(button_8_out));
  S_R_Flip_Flop #(.trigger("high")) s_r_ff_7 (
    .S(button_7_out), .clk(Cl0ck), .R(undriven_3), .Q(s_r_ff_8_q[1]), .reset(Reset));  // open: Qn, preset
  S_R_Flip_Flop #(.trigger("high")) s_r_ff_8 (
    .S(button_8_out), .clk(Cl0ck), .R(undriven_3), .Q(s_r_ff_8_q[0]), .reset(Reset));  // open: Qn, preset

  // Notes on the sheet:
  //   <Processor     Input Output Devices>
  //   Data Bus
  //   (IO Bus)
  //   Address Bus
  //   Keyboard
  //   Joystick
  //   Switches
  //   Buttons
endmodule

module Shifter_Circuit (
  input  Select_Immediate,
  input  [31:0] B_Bus_In,
  input  [31:0] Immediate_In,
  input  [4:0] Operation_Select,
  input  Write,
  input  [31:0] A_Bus_In,
  input  Clock,
  output [31:0] C_Bus_Out
);

  wire [4:0] multiplexer_1_out, Shift_Amount_Latch_q;
  wire [31:0] Shift_In_Latch_q, shifter_1_out, shifter_2_out, shifter_3_out;

  Multiplexer #(.width(5)) multiplexer_1 (
    .in0(B_Bus_In[4:0]), .in1(Immediate_In[4:0]), .out(multiplexer_1_out), .sel(Select_Immediate));
  Register #(.width(5)) Shift_Amount_Latch (
    .D(multiplexer_1_out), .en(Write), .clk(Clock), .Q(Shift_Amount_Latch_q));  // open: clr
  Register #(.width(32)) Shift_In_Latch (.D(A_Bus_In), .en(Write), .clk(Clock), .Q(Shift_In_Latch_q));  // open: clr
  Shifter #(.width(32)) shifter_1 (.in(Shift_In_Latch_q), .\dist (Shift_Amount_Latch_q), .out(shifter_1_out));
  Shifter #(.shift("lr"), .width(32)) shifter_2 (
    .in(Shift_In_Latch_q), .\dist (Shift_Amount_Latch_q), .out(shifter_2_out));
  Shifter #(.shift("ar"), .width(32)) shifter_3 (
    .in(Shift_In_Latch_q), .\dist (Shift_Amount_Latch_q), .out(shifter_3_out));
  Multiplexer #(.select(2), .width(32)) multiplexer_2 (
    .in0(shifter_1_out), .in1(shifter_2_out), .in2(shifter_3_out), .in3(shifter_3_out), .out(C_Bus_Out),
    .sel({Operation_Select[4], Operation_Select[2]}));
endmodule

module Address_ALU (
  input  Use_PC,
  input  [31:0] Source1,
  input  [31:0] Program_Counter_In,
  input  [31:0] Immediate,
  output [31:0] Result
);

  wire [31:0] multiplexer_1_out;

  Multiplexer #(.width(32)) multiplexer_1 (
    .in0(Source1), .in1(Program_Counter_In), .out(multiplexer_1_out), .sel(Use_PC));
  Adder #(.width(32)) adder_1 (.a(multiplexer_1_out), .b(Immediate), .out(Result));  // open: cin, cout

  // Notes on the sheet:
  //   Source1: initial=0xffffffff
endmodule

module ALU (
  input  [4:0] Operation,
  input  Use_PC,
  input  [31:0] a,
  input  [31:0] Program_Counter_In,
  input  Use_Immediate,
  input  [31:0] b,
  input  [31:0] Immediate,
  output [3:0] CNZV,
  output [31:0] Result,
  output [31:0] Source1,
  output [31:0] Source2
);

  wire and_1_out, comparator_1_lt, comparator_2_lt, or_1_out, xnor_1_out, xor_3_out, xor_4_out;
  wire [1:0] and_3_out;
  wire [1:1] and_2_out;
  wire [31:0] adder_1_out, and_4_out, bit_extender_1_out, bit_extender_2_out, bit_extender_3_out,
       multiplexer_3_out, multiplication_1_r_high, multiplication_1_r_low, or_2_out, shifter_1_out,
       shifter_2_out, shifter_3_out, xor_1_out, xor_2_out;

  or or_1 (or_1_out, Operation[2], ~Operation[4]);  // OR_Gate
  Multiplexer #(.width(32)) multiplexer_1 (.in0(a), .in1(Program_Counter_In), .out(Source1), .sel(Use_PC));
  Multiplexer #(.width(32)) multiplexer_2 (.in0(b), .in1(Immediate), .out(Source2), .sel(Use_Immediate));
  and and_1 (and_1_out, Operation[0], ~Operation[1], ~Operation[3], or_1_out);  // AND_Gate
  and and_2 (and_2_out[1], ~and_1_out, Use_Immediate);  // AND_Gate
  assign and_3_out = Operation[4:3] & ~{2{and_2_out[1]}};  // AND_Gate and_3, 2 bits wide
  assign or_2_out = Source1 | Source2;  // OR_Gate or_2, 32 bits wide
  assign and_4_out = Source1 & Source2;  // AND_Gate and_4, 32 bits wide
  assign bit_extender_1_out = {{31{and_3_out[1]}}, and_3_out[1]};  // Bit_Extender bit_extender_1
  Shifter #(.width(32)) shifter_1 (.in(Source1), .\dist (Source2[4:0]), .out(shifter_1_out));
  assign bit_extender_2_out = {{31{1'b0}}, comparator_1_lt};  // Bit_Extender bit_extender_2
  Comparator #(.width(32)) comparator_1 (.a(Source1), .b(Source2), .lt(comparator_1_lt));  // open: gt, eq
  assign bit_extender_3_out = {{31{1'b0}}, comparator_2_lt};  // Bit_Extender bit_extender_3
  Comparator #(.mode("unsigned"), .width(32)) comparator_2 (
    .a(Source1), .b(Source2), .lt(comparator_2_lt));  // open: gt, eq
  assign xor_1_out = Source1 ^ Source2;  // XOR_Gate xor_1, 32 bits wide
  Shifter #(.shift("lr"), .width(32)) shifter_2 (.in(Source1), .\dist (Source2[4:0]), .out(shifter_2_out));
  Shifter #(.shift("ar"), .width(32)) shifter_3 (.in(Source1), .\dist (Source2[4:0]), .out(shifter_3_out));
  Multiplication multiplication_1 (
    .Sign(Operation[1:0]), .A(Source1), .B(Source2), .R_Low(multiplication_1_r_low),
    .R_High(multiplication_1_r_high));
  Adder #(.width(32)) adder_1 (.a(Source1), .b(xor_2_out), .out(adder_1_out), .cin(and_3_out[1]), .cout(CNZV[0]));
  assign xor_2_out = bit_extender_1_out ^ Source2;  // XOR_Gate xor_2, 32 bits wide
  Multiplexer #(.width(32)) multiplexer_3 (
    .in0(shifter_2_out), .in1(shifter_3_out), .out(multiplexer_3_out), .sel(and_3_out[1]));
  Multiplexer #(.select(4), .width(32)) multiplexer_4 (
    .in0(adder_1_out), .in1(shifter_1_out), .in2(bit_extender_2_out), .in3(bit_extender_3_out),
    .in4(xor_1_out), .in5(multiplexer_3_out), .in6(or_2_out), .in7(and_4_out), .in8(multiplication_1_r_low),
    .in9(multiplication_1_r_high), .in10(multiplication_1_r_high), .in11(multiplication_1_r_high),
    .in12({32{1'b0}}), .in13({32{1'b0}}), .in14({32{1'b0}}), .in15({32{1'b0}}),
    .out({CNZV[1], Result[30:0]}), .sel({and_3_out[0], Operation[2:0]}));
  xor xor_3 (xor_3_out, CNZV[1], Source1[31]);
  xnor xnor_1 (xnor_1_out, Source1[31], Source2[31]);
  nor nor_1 (CNZV[2], Result[0], Result[1], Result[2], Result[3], Result[4], Result[5], Result[6], Result[7], Result[8], Result[9], Result[10], Result[11], Result[12], Result[13], Result[14], Result[15], Result[16], Result[17], Result[18], Result[19], Result[20], Result[21], Result[22], Result[23], Result[24], Result[25], Result[26], Result[27], Result[28], Result[29], Result[30], CNZV[1]);
  xor xor_4 (xor_4_out, xnor_1_out, and_3_out[1]);
  and and_5 (CNZV[3], xor_3_out, xor_4_out);

  assign Result[31] = CNZV[1];

  // Notes on the sheet:
  //   a: initial=0xffffffff
  //   if(~(operation == 1 | operation == 5 | operation = 21) & use_immediate) operation[4:3] = 2'b0
  //   \/
endmodule

module Program_Counter (
  input  Write,
  input  Jump,
  input  Reset,
  input  Clock,
  input  PC_Relative,
  input  [31:0] Address_In,
  input  [31:0] Immediate,
  input  Use_Offset,
  input  Forward_Address,
  output [31:0] Last_Out,
  output [31:0] Current_Out,
  output [31:0] Next_Out,
  output [31:0] Address_Bus_Out,
  output [1:0] Byte_Offset
);

  wire and_1_out;
  wire [1:0] and_2_out;
  wire [31:0] adder_1_out, multiplexer_1_out;

  Multiplexer #(.width(32)) multiplexer_1 (
    .in0(Address_In), .in1({Current_Out[31:2], 2'b00}), .out(multiplexer_1_out), .sel(PC_Relative));
  Adder #(.width(32)) adder_1 (.a(multiplexer_1_out), .b(Immediate), .out(adder_1_out));  // open: cin, cout
  Counter #(.max('h3fffffff), .width(30)) Next_Counter (
    .load(Jump), .D(adder_1_out[31:2]), .count(and_1_out), .Q(Next_Out[31:2]), .clk(Clock), .clr(Reset));  // open: carry, up
  and and_1 (and_1_out, Write, ~Jump);  // AND_Gate
  assign and_2_out = adder_1_out[1:0] & {2{Use_Offset}};  // AND_Gate and_2, 2 bits wide
  Register #(.width(2)) Byte_Offset_Reg (
    .D(adder_1_out[1:0]), .en(Forward_Address), .clk(Clock), .Q(Byte_Offset), .clr(Reset));
  Register #(.width(30)) Current (.D(Next_Out[31:2]), .en(Write), .clk(Clock), .Q(Current_Out[31:2]), .clr(Reset));
  Multiplexer #(.width(32)) multiplexer_2 (
    .in0({Next_Out[31:2], 2'b00}), .in1({adder_1_out[31:2], and_2_out}), .out(Address_Bus_Out),
    .sel(Forward_Address));
  Register #(.width(30)) Last (.D(Current_Out[31:2]), .en(Write), .clk(Clock), .Q(Last_Out[31:2]), .clr(Reset));

  assign Current_Out[1:0] = 2'b00;
  assign Last_Out[1:0] = 2'b00;
  assign Next_Out[1:0] = 2'b00;

  // Other names for the same wires on the sheet: Current_PC[31:2] = Current_Out[31:2]
endmodule

module Data_Input_Output (
  input  [31:0] CPU_In,
  input  Store,
  input  [2:0] Data_Type,
  input  [1:0] Data_Offset,
  input  [31:0] IO_In,
  input  Load,
  input  Clock,
  output [31:0] IO_Out,
  output [31:0] CPU_Out
);

  wire and_1_out, and_2_out, not_1_out;
  wire [7:0] Input_Register_q, Input_Register_q_2, Input_Register_q_3, Input_Register_q_4, multiplexer_1_out;
  wire [15:0] multiplexer_2_out, multiplexer_3_out;
  wire [31:0] bit_extender_1_out, bit_extender_2_out, multiplexer_4_out;

  Register #(.width(32)) Output_Register (.D(CPU_In), .en(Store), .clk(Clock), .Q(IO_Out));  // open: clr
  Register #(.width(32)) Input_Register (
    .D(IO_In), .en(Load), .clk(Clock),
    .Q({Input_Register_q_4, Input_Register_q_3, Input_Register_q_2, Input_Register_q}));  // open: clr
  Multiplexer #(.select(2), .width(8)) multiplexer_1 (
    .in0(Input_Register_q), .in1(Input_Register_q_2), .in2(Input_Register_q_3), .in3(Input_Register_q_4),
    .out(multiplexer_1_out), .sel(Data_Offset));
  Multiplexer #(.width(16)) multiplexer_2 (
    .in0({Input_Register_q_2, Input_Register_q}), .in1({Input_Register_q_3, Input_Register_q_2}),
    .out(multiplexer_2_out), .sel(Data_Offset[0]));
  Multiplexer #(.width(16)) multiplexer_3 (
    .in0(multiplexer_2_out), .in1({Input_Register_q_4, Input_Register_q_3}), .out(multiplexer_3_out),
    .sel(Data_Offset[1]));
  not not_1 (not_1_out, Data_Type[2]);
  and and_1 (and_1_out, multiplexer_1_out[7], not_1_out);
  assign bit_extender_1_out = {{24{and_1_out}}, multiplexer_1_out};  // Bit_Extender bit_extender_1
  and and_2 (and_2_out, multiplexer_3_out[15], not_1_out);
  assign bit_extender_2_out = {{16{and_2_out}}, multiplexer_3_out};  // Bit_Extender bit_extender_2
  Multiplexer #(.width(32)) multiplexer_4 (
    .in0(bit_extender_1_out), .in1(bit_extender_2_out), .out(multiplexer_4_out), .sel(Data_Type[0]));
  Multiplexer #(.width(32)) multiplexer_5 (
    .in0(multiplexer_4_out),
    .in1({Input_Register_q_4, Input_Register_q_3, Input_Register_q_2, Input_Register_q}), .out(CPU_Out),
    .sel(Data_Type[1]));

  // Notes on the sheet:
  //   IO_In: initial=0xf2f2f2f2
  //   CPU_In: initial=0xe3e3e3e3
endmodule

module Register_File (
  input  [14:0] Addresses_In,
  input  [31:0] C_Bus_In,
  input  Write,
  input  Clock,
  input  Reset,
  output [31:0] A_Bus_Out,
  output [31:0] B_Bus_Out
);

  Register_Bank IntRegisterBank (
    .Address_A(Addresses_In[9:5]), .Address_B(Addresses_In[14:10]), .Data_In(C_Bus_In), .Clock(Clock),
    .Address_C(Addresses_In[4:0]), .Write_Enable(Write), .Reset(Reset), .A_Data_Out(A_Bus_Out),
    .B_Data_Out(B_Bus_Out));
endmodule

module Register_Bank (
  input  [4:0] Address_A,
  input  Reset,
  input  [31:0] Data_In,
  input  Clock,
  input  [4:0] Address_C,
  input  [4:0] Address_B,
  input  Write_Enable,
  output [31:0] A_Data_Out,
  output [31:0] B_Data_Out
);

  wire [31:0] decoder_1_out0, x1_q, x2_q, x3_q, x4_q, x5_q, x6_q, x7_q, x8_q, x9_q, x10_q, x11_q, x12_q,
       x13_q, x14_q, x15_q, x16_q, x17_q, x18_q, x19_q, x20_q, x21_q, x22_q, x23_q, x24_q, x25_q, x26_q,
       x27_q, x28_q, x29_q, x30_q, x31_q;

  Decoder #(.select(5)) decoder_1 (
    .out0(decoder_1_out0[0]), .out1(decoder_1_out0[1]), .out2(decoder_1_out0[2]), .out3(decoder_1_out0[3]),
    .out4(decoder_1_out0[4]), .out5(decoder_1_out0[5]), .out6(decoder_1_out0[6]), .out7(decoder_1_out0[7]),
    .out8(decoder_1_out0[8]), .out9(decoder_1_out0[9]), .out10(decoder_1_out0[10]),
    .out11(decoder_1_out0[11]), .out12(decoder_1_out0[12]), .out13(decoder_1_out0[13]),
    .out14(decoder_1_out0[14]), .out15(decoder_1_out0[15]), .out16(decoder_1_out0[16]),
    .out17(decoder_1_out0[17]), .out18(decoder_1_out0[18]), .out19(decoder_1_out0[19]),
    .out20(decoder_1_out0[20]), .out21(decoder_1_out0[21]), .out22(decoder_1_out0[22]),
    .out23(decoder_1_out0[23]), .out24(decoder_1_out0[24]), .out25(decoder_1_out0[25]),
    .out26(decoder_1_out0[26]), .out27(decoder_1_out0[27]), .out28(decoder_1_out0[28]),
    .out29(decoder_1_out0[29]), .out30(decoder_1_out0[30]), .out31(decoder_1_out0[31]), .sel(Address_C),
    .en(Write_Enable));
  // NoConnect on Data_In
  // NoConnect on decoder_1_out0[0]
  // NoConnect on Clock
  Register #(.width(32)) x2 (.D(Data_In), .en(decoder_1_out0[2]), .clk(Clock), .Q(x2_q), .clr(Reset));
  Register #(.width(32)) x4 (.D(Data_In), .en(decoder_1_out0[4]), .clk(Clock), .Q(x4_q), .clr(Reset));
  Register #(.width(32)) x6 (.D(Data_In), .en(decoder_1_out0[6]), .clk(Clock), .Q(x6_q), .clr(Reset));
  Register #(.width(32)) x8 (.D(Data_In), .en(decoder_1_out0[8]), .clk(Clock), .Q(x8_q), .clr(Reset));
  Register #(.width(32)) x10 (.D(Data_In), .en(decoder_1_out0[10]), .clk(Clock), .Q(x10_q), .clr(Reset));
  Register #(.width(32)) x12 (.D(Data_In), .en(decoder_1_out0[12]), .clk(Clock), .Q(x12_q), .clr(Reset));
  Register #(.width(32)) x14 (.D(Data_In), .en(decoder_1_out0[14]), .clk(Clock), .Q(x14_q), .clr(Reset));
  Register #(.width(32)) x16 (.D(Data_In), .en(decoder_1_out0[16]), .clk(Clock), .Q(x16_q), .clr(Reset));
  Register #(.width(32)) x18 (.D(Data_In), .en(decoder_1_out0[18]), .clk(Clock), .Q(x18_q), .clr(Reset));
  Register #(.width(32)) x20 (.D(Data_In), .en(decoder_1_out0[20]), .clk(Clock), .Q(x20_q), .clr(Reset));
  Register #(.width(32)) x22 (.D(Data_In), .en(decoder_1_out0[22]), .clk(Clock), .Q(x22_q), .clr(Reset));
  Register #(.width(32)) x24 (.D(Data_In), .en(decoder_1_out0[24]), .clk(Clock), .Q(x24_q), .clr(Reset));
  Register #(.width(32)) x26 (.D(Data_In), .en(decoder_1_out0[26]), .clk(Clock), .Q(x26_q), .clr(Reset));
  Register #(.width(32)) x28 (.D(Data_In), .en(decoder_1_out0[28]), .clk(Clock), .Q(x28_q), .clr(Reset));
  Register #(.width(32)) x30 (.D(Data_In), .en(decoder_1_out0[30]), .clk(Clock), .Q(x30_q), .clr(Reset));
  Register #(.width(32)) x1 (.D(Data_In), .en(decoder_1_out0[1]), .clk(Clock), .Q(x1_q), .clr(Reset));
  Register #(.width(32)) x3 (.D(Data_In), .en(decoder_1_out0[3]), .clk(Clock), .Q(x3_q), .clr(Reset));
  Register #(.width(32)) x5 (.D(Data_In), .en(decoder_1_out0[5]), .clk(Clock), .Q(x5_q), .clr(Reset));
  Register #(.width(32)) x7 (.D(Data_In), .en(decoder_1_out0[7]), .clk(Clock), .Q(x7_q), .clr(Reset));
  Register #(.width(32)) x9 (.D(Data_In), .en(decoder_1_out0[9]), .clk(Clock), .Q(x9_q), .clr(Reset));
  Register #(.width(32)) x11 (.D(Data_In), .en(decoder_1_out0[11]), .clk(Clock), .Q(x11_q), .clr(Reset));
  Register #(.width(32)) x13 (.D(Data_In), .en(decoder_1_out0[13]), .clk(Clock), .Q(x13_q), .clr(Reset));
  Register #(.width(32)) x15 (.D(Data_In), .en(decoder_1_out0[15]), .clk(Clock), .Q(x15_q), .clr(Reset));
  Register #(.width(32)) x17 (.D(Data_In), .en(decoder_1_out0[17]), .clk(Clock), .Q(x17_q), .clr(Reset));
  Register #(.width(32)) x19 (.D(Data_In), .en(decoder_1_out0[19]), .clk(Clock), .Q(x19_q), .clr(Reset));
  Register #(.width(32)) x21 (.D(Data_In), .en(decoder_1_out0[21]), .clk(Clock), .Q(x21_q), .clr(Reset));
  Register #(.width(32)) x23 (.D(Data_In), .en(decoder_1_out0[23]), .clk(Clock), .Q(x23_q), .clr(Reset));
  Register #(.width(32)) x25 (.D(Data_In), .en(decoder_1_out0[25]), .clk(Clock), .Q(x25_q), .clr(Reset));
  Register #(.width(32)) x27 (.D(Data_In), .en(decoder_1_out0[27]), .clk(Clock), .Q(x27_q), .clr(Reset));
  Register #(.width(32)) x29 (.D(Data_In), .en(decoder_1_out0[29]), .clk(Clock), .Q(x29_q), .clr(Reset));
  Register #(.width(32)) x31 (.D(Data_In), .en(decoder_1_out0[31]), .clk(Clock), .Q(x31_q), .clr(Reset));
  Multiplexer #(.select(5), .width(32)) multiplexer_1 (
    .in0({32{1'b0}}), .in1(x1_q), .in2(x2_q), .in3(x3_q), .in4(x4_q), .in5(x5_q), .in6(x6_q), .in7(x7_q),
    .in8(x8_q), .in9(x9_q), .in10(x10_q), .in11(x11_q), .in12(x12_q), .in13(x13_q), .in14(x14_q),
    .in15(x15_q), .in16(x16_q), .in17(x17_q), .in18(x18_q), .in19(x19_q), .in20(x20_q), .in21(x21_q),
    .in22(x22_q), .in23(x23_q), .in24(x24_q), .in25(x25_q), .in26(x26_q), .in27(x27_q), .in28(x28_q),
    .in29(x29_q), .in30(x30_q), .in31(x31_q), .out(A_Data_Out), .sel(Address_A));
  Multiplexer #(.select(5), .width(32)) multiplexer_2 (
    .in0({32{1'b0}}), .in1(x1_q), .in2(x2_q), .in3(x3_q), .in4(x4_q), .in5(x5_q), .in6(x6_q), .in7(x7_q),
    .in8(x8_q), .in9(x9_q), .in10(x10_q), .in11(x11_q), .in12(x12_q), .in13(x13_q), .in14(x14_q),
    .in15(x15_q), .in16(x16_q), .in17(x17_q), .in18(x18_q), .in19(x19_q), .in20(x20_q), .in21(x21_q),
    .in22(x22_q), .in23(x23_q), .in24(x24_q), .in25(x25_q), .in26(x26_q), .in27(x27_q), .in28(x28_q),
    .in29(x29_q), .in30(x30_q), .in31(x31_q), .out(B_Data_Out), .sel(Address_B));
endmodule

module Operation_Controller (
  input  Phase1,
  input  Phase2,
  input  Phase3,
  input  [31:0] Data_In,
  input  Clock,
  input  Reset,
  input  [3:0] CNZV,
  output [14:0] Register_Adresses,
  output ALU_Use_PC,
  output [4:0] OP_Function,
  output [2:0] Funct3,
  output Register_File_Write,
  output Use_Immediate,
  output [6:0] OPCode,
  output PC_Read_Next,
  output PC_Jump,
  output Data_IO_Write_IO,
  output Data_IO_Read_IO,
  output IO_Load,
  output [31:0] Immediate,
  output PC_Relative,
  output PC_Use_Offset,
  output PAD_Read,
  output PAD_Write,
  output PC_Forward_Address,
  output PAD_Write_Address,
  output [1:0] PAD_Data_Size,
  output Load_Upper_Immediate
);

  wire and_1_out, and_2_out, and_3_out, and_6_out, and_9_out, Branch, Floating_Point, Flush_Next_Instruction,
       Immediate_t, Jump_PC_Relative, Jump_Register_Relative, Load, Load_Second_Part, Load_Upper_Immediate_t,
       multiplexer_4_out, not_1_out, not_2_out, not_3_out, Operation, or_1_out, or_2_out, or_3_out, or_5_out,
       or_7_out, or_10_out, s_r_ff_1_qn, Store_Second_Part, System, xor_1_out;
  wire [4:0] multiplexer_5_out;
  wire [4:4] not_4_out;
  wire [6:0] Funct7;
  wire [31:0] Last_Instruction_q, multiplexer_1_out, Next_Instruction_q;
  wire [31:7] Current_Instruction_q;

  Register #(.width(32)) Next_Instruction (.D(Data_In), .en(Phase2), .clk(Clock), .Q(Next_Instruction_q), .clr(Reset));
  S_R_Flip_Flop #(.trigger("falling")) s_r_ff_1 (
    .S(Flush_Next_Instruction), .R(Phase2), .clk(Clock), .Qn(s_r_ff_1_qn));  // open: Q, reset, preset
  Multiplexer #(.width(32)) multiplexer_1 (
    .in0(32'h13), .in1(Next_Instruction_q), .out(multiplexer_1_out), .sel(s_r_ff_1_qn));
  Register #(.trigger("falling"), .width(32)) Current_Instruction (
    .D(multiplexer_1_out), .en(Phase1), .clk(Clock), .Q({Current_Instruction_q, OPCode}), .clr(Reset));
  Register #(.trigger("falling"), .width(32)) Last_Instruction (
    .D({Current_Instruction_q, OPCode}), .en(Phase1), .clk(Clock), .Q(Last_Instruction_q), .clr(Reset));
  Multiplexer #(.width(15)) multiplexer_2 (
    .in0({Current_Instruction_q[24:15], Current_Instruction_q[11:7]}),
    .in1({Last_Instruction_q[24:15], Last_Instruction_q[11:7]}), .out(Register_Adresses), .sel(and_1_out));
  and and_1 (and_1_out, Load_Second_Part, Phase2);
  or or_1 (or_1_out, and_1_out, and_2_out);
  and and_2 (and_2_out, Store_Second_Part, Phase1);
  Multiplexer #(.width(10)) multiplexer_3 (
    .in0({Current_Instruction_q[31:25], Current_Instruction_q[14:12]}),
    .in1({Last_Instruction_q[31:25], Last_Instruction_q[14:12]}), .out({Funct7, Funct3}), .sel(or_1_out));
  or or_2 (or_2_out, ALU_Use_PC, Load_Upper_Immediate_t);
  Load_Store_Decoder LoadStoreDecoder (
    .OPCODE(Last_Instruction_q[6:0]), .STORE(Store_Second_Part), .LOAD(Load_Second_Part));
  Operation_Decoder OperationDecoder (
    .OPCODE(OPCode), .IMMEDIATE(Immediate_t), .LOAD(Load), .OPERATION(Operation),
    .ADD_UPPER_IMMEDIATE_PC(ALU_Use_PC), .STORE(PC_Use_Offset),
    .LOAD_UPPER_IMMEDIATE(Load_Upper_Immediate_t), .BRANCH(Branch),
    .JUMP_AND_LINK_REGISTER(Jump_Register_Relative), .JUMP_AND_LINK(Jump_PC_Relative), .SYSTEM(System),
    .FLOATING_POINT(Floating_Point));
  Immediate_Decoder ImmediateDecoder (
    .Upper_Immediate(or_2_out), .Jump(Jump_PC_Relative), .Branch(Branch),
    .Instruction({Current_Instruction_q, OPCode}), .Store(PC_Use_Offset), .Immediate(Immediate));
  or or_3 (or_3_out, Load_Upper_Immediate_t, ALU_Use_PC, Operation, Load, Jump_PC_Relative, Jump_Register_Relative, System);
  and and_3 (and_3_out, Phase3, or_3_out);
  or or_4 (Register_File_Write, and_3_out, and_6_out);
  or or_5 (or_5_out, Jump_Register_Relative, Jump_PC_Relative);
  and and_4 (PC_Read_Next, or_5_out, Phase3);
  xor xor_1 (xor_1_out, CNZV[3], CNZV[1]);
  or or_6 (PC_Relative, Branch, Jump_PC_Relative);
  or or_7 (or_7_out, Load, PC_Use_Offset);
  and and_5 (PC_Forward_Address, or_7_out, Phase3);
  and and_6 (and_6_out, Phase2, Load_Second_Part);
  not not_1 (not_1_out, CNZV[2]);
  Multiplexer #(.enable("true"), .select(3)) multiplexer_4 (
    .in0(CNZV[2]), .in1(not_1_out), .in2(1'b0), .in3(1'b0), .in4(xor_1_out), .in5(not_2_out),
    .in6(not_3_out), .in7(CNZV[0]), .out(multiplexer_4_out), .sel(Funct3), .en(Branch));
  not not_2 (not_2_out, xor_1_out);
  not not_3 (not_3_out, CNZV[0]);
  and and_7 (Load_Upper_Immediate, Load_Upper_Immediate_t, Phase3);
  or or_8 (Flush_Next_Instruction, multiplexer_4_out, Jump_Register_Relative, Jump_PC_Relative);
  and and_8 (PC_Jump, Flush_Next_Instruction, Phase3);
  or or_9 (Use_Immediate, Immediate_t, ALU_Use_PC);
  or or_10 (or_10_out, Load, PC_Use_Offset);
  and and_9 (and_9_out, or_10_out, Phase3);
  or or_11 (PAD_Write_Address, and_9_out, Phase1);
  not not_4 (not_4_out[4], Funct3[2]);
  Multiplexer #(.width(5)) multiplexer_5 (
    .in0({not_4_out[4], 4'b0101}), .in1(5'b10000), .out(multiplexer_5_out), .sel(Branch));
  Multiplexer #(.width(5)) multiplexer_6 (
    .in0(multiplexer_5_out), .in1({Funct7[5], Funct7[1], Funct3}), .out(OP_Function), .sel(Operation));
  and and_10 (Data_IO_Write_IO, Phase1, Load_Second_Part);
  or or_12 (PAD_Read, Phase2, Data_IO_Write_IO);
  and and_11 (Data_IO_Read_IO, Phase1, Store_Second_Part);
  or or_13 (PAD_Data_Size[0], Funct3[0], Funct3[1]);
  and and_12 (IO_Load, Phase2, Load_Second_Part);

  assign PAD_Data_Size[1] = Funct3[1];
  assign PAD_Write = Data_IO_Read_IO;

  // Other names for the same wires on the sheet: Funct10[9:0] = {Funct7, Funct3}; Add_Upper_Immediate_PC = ALU_Use_PC;
  //   Phase1n = Phase1; Phase2n = Phase2; Phase3n = Phase3; Store = PC_Use_Offset

  // Notes on the sheet:
  //   TODO: Investigar o porque aqui precisa estar invertido =>
  //   Register File
  //   Program Counter
  //   Misc
  //   ALU And Shifter
  //   Input/Output and interface Pads
endmodule

module Operation_Decoder (
  input  [6:0] OPCODE,
  output FLOATING_POINT,
  output IMMEDIATE,
  output LOAD,
  output OPERATION,
  output ADD_UPPER_IMMEDIATE_PC,
  output STORE,
  output LOAD_UPPER_IMMEDIATE,
  output BRANCH,
  output JUMP_AND_LINK_REGISTER,
  output JUMP_AND_LINK,
  output SYSTEM
);

  wire not_1_out, not_2_out, not_3_out, not_4_out, not_5_out, or_1_out, or_2_out, or_3_out, or_4_out;

  not not_1 (not_1_out, OPCODE[6]);
  not not_2 (not_2_out, OPCODE[5]);
  not not_3 (not_3_out, OPCODE[4]);
  not not_4 (not_4_out, OPCODE[3]);
  not not_5 (not_5_out, OPCODE[2]);
  or or_1 (or_1_out, OPCODE[6], not_3_out);
  or or_2 (or_2_out, not_1_out, not_2_out);
  or or_3 (or_3_out, OPCODE[4], OPCODE[2]);
  and and_1 (IMMEDIATE, not_2_out, not_1_out, not_5_out);
  and and_2 (LOAD, not_3_out, not_2_out);
  or or_4 (or_4_out, not_1_out, not_2_out);
  and and_3 (ADD_UPPER_IMMEDIATE_PC, OPCODE[2], OPCODE[4], not_2_out);
  and and_4 (STORE, OPCODE[5], not_3_out, not_1_out);
  and and_5 (LOAD_UPPER_IMMEDIATE, OPCODE[2], OPCODE[5], OPCODE[4]);
  and and_6 (BRANCH, OPCODE[6], not_3_out, not_5_out);
  and and_7 (JUMP_AND_LINK_REGISTER, OPCODE[2], not_4_out, OPCODE[6]);
  and and_8 (JUMP_AND_LINK, OPCODE[3], OPCODE[6]);
  and and_9 (SYSTEM, OPCODE[6], OPCODE[5], OPCODE[4]);
  and and_10 (FLOATING_POINT, or_1_out, or_2_out, or_3_out);
  and and_11 (OPERATION, OPCODE[4], or_4_out, not_5_out);
endmodule

module Immediate_Decoder (
  input  Upper_Immediate,
  input  Jump,
  input  Branch,
  input  Store,
  input  [31:0] Instruction,
  output [31:0] Immediate
);

  wire [1:0] or_2_out;
  wire [11:0] multiplexer_1_out;
  wire [31:0] bit_extender_1_out, bit_extender_2_out, bit_extender_3_out;

  Multiplexer #(.width(12)) multiplexer_1 (
    .in0(Instruction[31:20]), .in1({Instruction[31:25], Instruction[11:7]}), .out(multiplexer_1_out),
    .sel(Store));
  assign bit_extender_1_out = {{19{Instruction[31]}}, {Instruction[31], Instruction[7], Instruction[30:25], Instruction[11:8], 1'b0}};  // Bit_Extender bit_extender_1
  assign bit_extender_2_out = {{11{Instruction[31]}}, {Instruction[31], Instruction[19:12], Instruction[20], Instruction[30:21], 1'b0}};  // Bit_Extender bit_extender_2
  assign bit_extender_3_out = {{20{multiplexer_1_out[11]}}, multiplexer_1_out};  // Bit_Extender bit_extender_3
  or or_1 (or_2_out[1], Upper_Immediate, Jump);
  or or_2 (or_2_out[0], Jump, Branch);
  Multiplexer #(.select(2), .width(32)) multiplexer_2 (
    .in0(bit_extender_3_out), .in1(bit_extender_1_out), .in2({Instruction[31:12], {12{1'b0}}}),
    .in3(bit_extender_2_out), .out(Immediate), .sel(or_2_out));

  // Notes on the sheet:
  //   I-type
  //   S-type
  //   B-type
  //   U-type
  //   J-type
endmodule

module Load_Store_Decoder (
  input  [6:0] OPCODE,
  output LOAD,
  output STORE
);

  wire and_2_out, and_3_out, not_1_out, not_2_out, not_3_out, not_4_out, not_5_out;

  not not_1 (not_1_out, OPCODE[6]);
  not not_2 (not_2_out, OPCODE[5]);
  not not_3 (not_3_out, OPCODE[4]);
  not not_4 (not_4_out, OPCODE[3]);
  not not_5 (not_5_out, OPCODE[2]);
  and and_1 (LOAD, not_1_out, not_2_out, not_3_out, not_4_out, OPCODE[1], OPCODE[0]);
  and and_2 (and_2_out, not_1_out, OPCODE[5], not_3_out, not_4_out, not_5_out, OPCODE[1], OPCODE[0]);
  and and_3 (and_3_out, not_1_out, OPCODE[5], not_3_out, OPCODE[3], OPCODE[2], OPCODE[1], OPCODE[0]);
  or or_1 (STORE, and_2_out, and_3_out);
endmodule

module Register_History_Generator (
  input  [31:0] Current_Value,
  input  [4:0] Current_Address,
  input  [4:0] Target_Address,
  input  Write_Signal,
  input  Reset,
  input  Clock,
  output Out_Clock,
  output [15:0] Out_Value
);

  wire and_1_out, comparator_1_eq, comparator_2_gt;
  wire [3:0] counter_1_q;
  wire [31:0] Last_Value_q, register_1_q;

  Comparator #(.width(5)) comparator_1 (.a(Current_Address), .b(Target_Address), .eq(comparator_1_eq));  // open: gt, lt
  and and_1 (and_1_out, comparator_1_eq, Write_Signal);
  Register #(.trigger("falling"), .width(32)) register_1 (
    .D(Current_Value), .en(and_1_out), .clk(Clock), .Q(register_1_q));  // open: clr
  Register #(.trigger("falling"), .width(32)) Last_Value (
    .D(Current_Value), .en(and_1_out), .clk(Clock), .Q(Last_Value_q), .clr(Reset));
  and and_2 (Out_Clock, and_1_out, Clock);
  Comparator #(.width(32)) comparator_2 (.a(register_1_q), .b(Last_Value_q), .gt(comparator_2_gt));  // open: eq, lt
  Counter #(.max('hf), .width(4)) counter_1 (
    .clr(Reset), .up(comparator_2_gt), .count(and_1_out), .clk(Clock), .Q(counter_1_q));  // open: load, D, carry
  Decoder #(.enable("false"), .select(4)) decoder_1 (
    .out0(Out_Value[0]), .out1(Out_Value[1]), .out2(Out_Value[2]), .out3(Out_Value[3]), .out4(Out_Value[4]),
    .out5(Out_Value[5]), .out6(Out_Value[6]), .out7(Out_Value[7]), .out8(Out_Value[8]), .out9(Out_Value[9]),
    .out10(Out_Value[10]), .out11(Out_Value[11]), .out12(Out_Value[12]), .out13(Out_Value[13]),
    .out14(Out_Value[14]), .out15(Out_Value[15]), .sel(counter_1_q));
endmodule

module F_ALU (
  input  [4:0] Operation,
  input  Write,
  input  Use_PC,
  input  [31:0] Source1,
  input  [31:0] Program_Counter_In,
  input  Use_Immediate,
  input  [31:0] Source2,
  input  [31:0] Immediate,
  input  Clock,
  input  in_10,
  output [31:0] Result,
  output [3:0] CNZV
);

  wire fpcomparator_1_p5, fpcomparator_1_p10, fpcomparator_1_p11, xor_1_out;
  wire [1:0] and_1_out;
  wire [7:0] slider_1_out, slider_2_out;
  wire [15:0] bit_extender_1_out, bit_extender_2_out;
  wire [31:0] fpcomparator_1_p4, fpcomparator_1_p8, fpcomparator_1_p9, inttofp_1_p2, inttofp_2_p2,
       multiplexer_1_out, multiplexer_2_out, multiplexer_3_out, multiplexer_4_out, Source_1_q, Source_2_q,
       undriven, undriven_2, undriven_3, undriven_4, undriven_5, undriven_6, undriven_7, undriven_8,
       undriven_9, undriven_10, undriven_11, undriven_12;

  Multiplexer #(.width(32)) multiplexer_1 (
    .in0(Source1), .in1(Program_Counter_In), .out(multiplexer_1_out), .sel(Use_PC));
  Multiplexer #(.width(32)) multiplexer_2 (
    .in0(Source2), .in1(Immediate), .out(multiplexer_2_out), .sel(Use_Immediate));
  Register #(.trigger("falling"), .width(32)) Source_1 (
    .D(multiplexer_1_out), .en(Write), .clk(Clock), .Q(Source_1_q));  // open: clr
  Register #(.trigger("falling"), .width(32)) Source_2 (
    .D(multiplexer_2_out), .en(Write), .clk(Clock), .Q(Source_2_q));  // open: clr
  assign bit_extender_1_out = {{8{1'b0}}, slider_1_out};  // Bit_Extender bit_extender_1
  Slider slider_1 (.out(slider_1_out));
  assign bit_extender_2_out = {{8{1'b0}}, slider_2_out};  // Bit_Extender bit_extender_2
  Slider slider_2 (.out(slider_2_out));
  // IntToFP #(.width(16)) inttofp_1: pin names not known; wires that end beside it: bit_extender_1_out, inttofp_1_p2
  // IntToFP #(.width(16)) inttofp_2: pin names not known; wires that end beside it: bit_extender_2_out, inttofp_2_p2
  // FPComparator fpcomparator_1: pin names not known; wires that end beside it: Source_2_q, Source_1_q, Source_2_q, fpcomparator_1_p4, fpcomparator_1_p5, inttofp_1_p2, inttofp_2_p2, fpcomparator_1_p8, fpcomparator_1_p9, fpcomparator_1_p10, fpcomparator_1_p11
  Multiplexer #(.width(32)) multiplexer_3 (
    .in0(inttofp_1_p2), .in1(inttofp_2_p2), .out(multiplexer_3_out), .sel(xor_1_out));
  xor xor_1 (xor_1_out, fpcomparator_1_p10, in_10);
  FPDivider fpdivider_1 ();  // open: a, b, out
  // Probe on multiplexer_3_out
  FPSubtractor fpsubtractor_1 ();  // open: a, b, out
  FPMultiplier fpmultiplier_1 ();  // open: a, b, out
  // FPToInt fptoint_1: pin names not known
  assign and_1_out = Operation[4:3] & ~{2{Use_Immediate}};  // AND_Gate and_1, 2 bits wide
  FPAdder fpadder_1 ();  // open: a, b, out
  Multiplexer #(.select(4), .width(32)) multiplexer_4 (
    .in0(undriven_2), .in1({32{1'b0}}), .in2(undriven), .in3(undriven_3), .in4(undriven_4), .in5({32{1'b0}}),
    .in6(undriven_5), .in7(undriven_6), .in8(undriven_7), .in9(undriven_8), .in10(undriven_9),
    .in11(undriven_10), .in12(undriven_11), .in13(fpcomparator_1_p8), .in14(undriven_12),
    .in15(fpcomparator_1_p4), .out(multiplexer_4_out), .sel({and_1_out[0], Operation[2:0]}));
  Multiplexer #(.width(32)) multiplexer_5 (
    .in0(multiplexer_4_out), .in1(fpcomparator_1_p9), .out({CNZV[1], Result[30:0]}), .sel(and_1_out[1]));
  Multiplexer multiplexer_6 (.in0(fpcomparator_1_p11), .in1(fpcomparator_1_p5), .out(CNZV[0]), .sel(and_1_out[1]));
  nor nor_1 (CNZV[2], Result[0], Result[1], Result[2], Result[3], Result[4], Result[5], Result[6], Result[7], Result[8], Result[9], Result[10], Result[11], Result[12], Result[13], Result[14], Result[15], Result[16], Result[17], Result[18], Result[19], Result[20], Result[21], Result[22], Result[23], Result[24], Result[25], Result[26], Result[27], Result[28], Result[29], Result[30], CNZV[1]);
  xor xor_2 (CNZV[3], CNZV[1], CNZV[0]);

  assign Result[31] = CNZV[1];

  // Notes on the sheet:
  //   Source1: initial=0xffffffff
endmodule

module Multiplication (
  input  [31:0] A,
  input  [31:0] B,
  input  [1:0] Sign,
  output [31:0] R_Low,
  output [31:0] R_High
);

  wire [32:31] multiplier_1_cout;
  wire [32:32] and_1_out, and_2_out;

  and and_1 (and_1_out[32], A[31], Sign[0]);
  and and_2 (and_2_out[32], B[31], Sign[1]);
  Multiplier #(.mode("twosComplement"), .width(33)) multiplier_1 (
    .a({and_1_out[32], A}), .b({and_2_out[32], B}), .out({R_High[0], R_Low}),
    .cout({multiplier_1_cout, R_High[31:1]}));  // open: cin
endmodule

module Address_Selector (
  input  Read_In,
  input  [31:0] Address_In,
  input  [31:0] Min_Address,
  input  [31:0] Max_Address,
  input  Write_In,
  output [31:0] Address_Out,
  output Read_Out,
  output Write_Out
);

  wire and_1_out, comparator_1_eq, comparator_1_gt, comparator_2_lt, or_1_out;

  Comparator #(.width(32)) comparator_1 (
    .a(Address_In), .b(Min_Address), .gt(comparator_1_gt), .eq(comparator_1_eq));  // open: lt
  Comparator #(.width(32)) comparator_2 (.a(Address_In), .b(Max_Address), .lt(comparator_2_lt));  // open: gt, eq
  or or_1 (or_1_out, comparator_1_gt, comparator_1_eq);
  and and_1 (and_1_out, or_1_out, comparator_2_lt);
  and and_2 (Read_Out, Read_In, and_1_out);
  and and_3 (Write_Out, and_1_out, Write_In);

  assign Address_Out = Address_In;
endmodule
